# Fritzing sketch supermaquina (saved by Fritzing 0.9.3b)
circuit board: 8.46667cm x 5.64444cm
breadboards: 1

parts:
  LED1 = LED - 5mm [color="Red (633nm)" package="5 mm [THT]"]
  R1 = Resistor [tolerance=±5% resistance=330 package=THT]
  Componente1 = Arduino Uno (Rev3)
  LED2 = LED - 5mm [color="Red (633nm)" package="5 mm [THT]"]
  R2 = Resistor [tolerance=±5% resistance=220 package=THT]
  R3 = Resistor [tolerance=±5% resistance=220 package=THT]
  LED3 = LED - 5mm [color="Red (633nm)" package="5 mm [THT]"]
  LED4 = LED - 5mm [color="Red (633nm)" package="5 mm [THT]"]
  LED5 = LED - 5mm [color="Red (633nm)" package="5 mm [THT]"]
  R4 = Resistor [tolerance=±5% resistance=220 package=THT]
  R5 = Resistor [tolerance=±5% resistance=220 package=THT]

nets:
  N1: LED1.cathode, R1.Pin_0
  N2: LED1.anode, Componente1.D13/SCK
  N3: R1.Pin_1, Componente1.GND, R2.Pin_1, R3.Pin_1, R4.Pin_1, R5.Pin_1
  N4: Componente1.D9_PWM, LED5.anode
  N5: Componente1.D10_PWM/SS, LED4.anode
  N6: Componente1.D11_PWM/MOSI, LED3.anode
  N7: Componente1.D12/MISO, LED2.anode
  N8: LED2.cathode, R2.Pin_0
  N9: R3.Pin_0, LED3.cathode
  N10: LED4.cathode, R4.Pin_0
  N11: LED5.cathode, R5.Pin_0

// code stored in the sketch: supermaquina.ino

